# Fritzing sketch sketch-02-light-sensor (saved by Fritzing 0.9.3b)
breadboards: 1

parts:
  Part1 = Arduino Leonardo (Rev3b)
  LED1 = LED - 5mm [color="Red (633nm)" package="5 mm [THT]"]

nets:
  N1: Part1.D11_PWM, LED1.cathode
  N2: Part1.D12/A11, LED1.anode
